// Logisim project Proj2starter.circ as structural Verilog: 4 circuits, main circuit regfile
module CPUmain (
  input  [31:0] in_1
);

  wire control_1_imm_sel, control_1_reg_write_e, undriven, undriven_2;
  wire [3:0] control_1_alu_code;
  wire [4:0] control_1_rd, control_1_rs, control_1_rt;
  wire [15:0] bit_extender_1_out;
  wire [31:0] alu_1_res, control_1_imm, multiplexer_1_out, multiplexer_2_out, ram_1_dout, regfile_1_rs_data,
       regfile_1_rt_data, shifter_1_out;

  ROM #(.addrWidth(16), .dataWidth(32)) rom_1 ();  // open: addr, data
  Multiplexer #(.width(32)) multiplexer_1 (.in0(alu_1_res), .in1(ram_1_dout), .out(multiplexer_1_out), .sel(undriven));
  regfile regfile_1 (
    .rd_data(multiplexer_1_out), .rd(control_1_rd), .write_e(control_1_reg_write_e), .rs(control_1_rs),
    .rt(control_1_rt), .rs_data(regfile_1_rs_data), .rt_data(regfile_1_rt_data));
  Control control_1 (
    .Inst(in_1), .rs(control_1_rs), .rt(control_1_rt), .rd(control_1_rd), .imm(control_1_imm),
    .reg_write_e(control_1_reg_write_e), .imm_sel(control_1_imm_sel), .ALU_code(control_1_alu_code));
  Multiplexer #(.width(32)) multiplexer_2 (
    .in0(regfile_1_rt_data), .in1(control_1_imm), .out(multiplexer_2_out), .sel(control_1_imm_sel));
  Shifter #(.shift("lr"), .width(32)) shifter_1 (.in(alu_1_res), .out(shifter_1_out));  // open: dist
  ALU alu_1 (.ALU_CODE(control_1_alu_code), .OP1(regfile_1_rs_data), .OP2(multiplexer_2_out), .Res(alu_1_res));
  Bit_Extender #(.in_width(32)) bit_extender_1 (.in(shifter_1_out), .out(bit_extender_1_out));
  RAM #(.addrWidth(16), .dataWidth(32)) ram_1 (
    .addr(bit_extender_1_out), .we(undriven_2), .clk(1'b1), .dout(ram_1_dout));  // open: oe, din
  // Pins of 1 and 3 bits meet at 3'b101
endmodule

module regfile (
  input  [4:0] rd,
  input  write_e,
  input  [4:0] rs,
  input  [4:0] rt,
  input  [31:0] rd_data,
  output [31:0] rs_data,
  output [31:0] rt_data
);
endmodule

module ALU (
  input  [3:0] ALU_CODE,
  input  [31:0] OP1,
  input  [31:0] OP2,
  output [31:0] Res
);

  wire clock_1_out, comparator_1_lt, comparator_2_eq, comparator_3_eq, or_2_out;
  wire [4:0] bit_extender_1_out, bit_extender_2_out;
  wire [31:0] adder_1_out, and_1_out, bit_extender_3_out, divider_1_out, divider_1_rem, HI_q, LO_q,
       multiplexer_1_out, multiplexer_2_out, multiplier_1_cout, multiplier_1_out, nor_1_out, or_1_out,
       shifter_1_out, shifter_2_out, subtractor_1_out, undriven;

  Bit_Extender #(.in_width(32), .out_width(5), .\type ("zero")) bit_extender_1 (.in(OP2), .out(bit_extender_1_out));
  Bit_Extender #(.in_width(32), .out_width(5), .\type ("zero")) bit_extender_2 (.in(OP2), .out(bit_extender_2_out));
  Adder #(.width(32)) adder_1 (.a(OP1), .b(OP2), .out(adder_1_out));  // open: cin, cout
  Subtractor #(.width(32)) subtractor_1 (.a(OP1), .b(OP2), .out(subtractor_1_out));  // open: bin, bout
  Shifter #(.width(32)) shifter_1 (.in(OP1), .\dist (bit_extender_1_out), .out(shifter_1_out));
  Shifter #(.shift("lr"), .width(32)) shifter_2 (.in(OP1), .\dist (bit_extender_2_out), .out(shifter_2_out));
  Comparator #(.width(32)) comparator_1 (.a(OP1), .b(OP2), .lt(comparator_1_lt));  // open: gt, eq
  assign and_1_out = OP1 & OP2;  // AND_Gate and_1, 32 bits wide
  assign or_1_out = OP1 | OP2;  // OR_Gate or_1, 32 bits wide
  assign nor_1_out = ~(OP1 | OP2);  // NOR_Gate nor_1, 32 bits wide
  // XOR_Gate xor_1 has open pins: in0=OP1, in1=OP2, out=open
  Multiplier #(.width(32)) multiplier_1 (
    .a(OP1), .b(OP2), .out(multiplier_1_out), .cout(multiplier_1_cout));  // open: cin
  Divider #(.width(32)) divider_1 (.a(OP1), .b(OP2), .out(divider_1_out), .rem(divider_1_rem));  // open: upper
  assign bit_extender_3_out = {{31{1'b0}}, comparator_1_lt};  // Bit_Extender bit_extender_3
  Multiplexer #(.width(32)) multiplexer_1 (
    .in0(multiplier_1_out), .in1(divider_1_out), .out(multiplexer_1_out), .sel(comparator_3_eq));
  Multiplexer #(.width(32)) multiplexer_2 (
    .in0(multiplier_1_cout), .in1(divider_1_rem), .out(multiplexer_2_out), .sel(comparator_3_eq));
  Comparator #(.width(4)) comparator_2 (.a(ALU_CODE), .b(4'b0010), .eq(comparator_2_eq));  // open: gt, lt
  Comparator #(.width(4)) comparator_3 (.a(ALU_CODE), .b(4'b0011), .eq(comparator_3_eq));  // open: gt, lt
  Clock clock_1 (.out(clock_1_out));
  or or_2 (or_2_out, comparator_2_eq, comparator_3_eq);
  Register #(.width(32)) LO (.D(multiplexer_1_out), .en(or_2_out), .clk(clock_1_out), .Q(LO_q));  // open: clr
  Register #(.width(32)) HI (.D(multiplexer_2_out), .en(or_2_out), .clk(clock_1_out), .Q(HI_q));  // open: clr
  Multiplexer #(.select(4), .width(32)) multiplexer_3 (
    .in0(adder_1_out), .in1(subtractor_1_out), .in4(LO_q), .in5(HI_q), .in6(shifter_1_out),
    .in7(shifter_2_out), .in8(bit_extender_3_out), .in9(and_1_out), .in10(or_1_out), .in11(nor_1_out),
    .in12(undriven), .out(Res), .sel(ALU_CODE));  // open: in2, in3, in13, in14, in15

  // Notes on the sheet:
  //   sll
  //   srl
  //   AND
  //   OR
  //   NOR
  //   XOR
  //   Overflow
  //   Quotient
  //   slt
  //   Product
  //   Remainder
endmodule

module Control (
  input  [31:0] Inst,
  output [4:0] rs,
  output [4:0] rt,
  output [4:0] rd,
  output [31:0] imm,
  output reg_write_e,
  output imm_sel,
  output [3:0] ALU_code
);
endmodule
