// Logisim project Project2.circ as structural Verilog: 4 circuits, main circuit regfile
module CPUmain (
  input  [31:0] instruction
);

  wire alu_1_equal, and_1_out, and_2_out, clock_1_out, clock_2_out, comparator_1_eq, comparator_2_eq,
       control_1_alu_memsel, control_1_imm_sel, control_1_is_beq, control_1_is_bne, control_1_is_j,
       control_1_reg_we, control_1_we_mem, not_1_out, or_1_out, or_3_out, undriven, undriven_2;
  wire [3:0] control_1_alu_code;
  wire [4:0] control_1_rd, control_1_rs, control_1_rt;
  wire [15:0] bit_extender_3_out, bit_extender_6_out, control_1_imm, multiplexer_8_out, shifter_1_out,
       shifter_4_out;
  wire [25:0] bit_extender_4_out, shifter_2_out;
  wire [31:0] adder_1_out, adder_2_out, alu_1_res, bit_extender_1_out, bit_extender_2_out,
       bit_extender_5_out, multiplexer_1_out, multiplexer_2_out, multiplexer_3_out, multiplexer_4_out,
       multiplexer_5_out, multiplexer_6_out, multiplexer_7_out, ram_1_dout, regfile_1_rs_data,
       regfile_1_rt_data, register_1_q, shifter_3_out, shifter_5_out;

  Shifter #(.width(16)) shifter_1 (.in(multiplexer_8_out), .\dist (4'b0010), .out(shifter_1_out));
  Shifter #(.width(26)) shifter_2 (.in(bit_extender_4_out), .\dist (5'b00010), .out(shifter_2_out));
  Adder #(.width(32)) adder_1 (.a(register_1_q), .b(32'h4), .out(adder_1_out));  // open: cin, cout
  assign bit_extender_1_out = {{16{shifter_1_out[15]}}, shifter_1_out};  // Bit_Extender bit_extender_1
  assign bit_extender_2_out = {{6{shifter_2_out[25]}}, shifter_2_out};  // Bit_Extender bit_extender_2
  Multiplexer #(.width(32)) multiplexer_1 (
    .in0(adder_1_out), .in1(adder_2_out), .out(multiplexer_1_out), .sel(or_1_out));
  Adder #(.width(32)) adder_2 (.a(adder_1_out), .b(bit_extender_1_out), .out(adder_2_out));  // open: cin, cout
  Multiplexer #(.width(32)) multiplexer_2 (
    .in0(bit_extender_2_out), .in1(regfile_1_rs_data), .out(multiplexer_2_out), .sel(undriven));
  Multiplexer #(.width(32)) multiplexer_3 (
    .in0(multiplexer_1_out), .in1(multiplexer_2_out), .out(multiplexer_3_out), .sel(control_1_is_j));
  Shifter #(.width(32)) shifter_3 (.in(register_1_q), .\dist (5'b00010), .out(shifter_3_out));
  Register #(.width(32)) register_1 (.D(multiplexer_3_out), .clk(clock_1_out), .Q(register_1_q));  // open: en, clr
  Clock clock_1 (.out(clock_1_out));
  Bit_Extender #(.in_width(32)) bit_extender_3 (.in(shifter_3_out), .out(bit_extender_3_out));
  ROM #(.addrWidth(16), .dataWidth(32)) rom_1 (.addr(bit_extender_3_out), .data(instruction));
  Bit_Extender #(.in_width(32), .out_width(26)) bit_extender_4 (.in(instruction), .out(bit_extender_4_out));
  Multiplexer #(.width(32)) multiplexer_4 (
    .in0(alu_1_res), .in1(ram_1_dout), .out(multiplexer_4_out), .sel(control_1_alu_memsel));
  Multiplexer #(.width(32)) multiplexer_5 (
    .in0(multiplexer_4_out), .in1(adder_1_out), .out(multiplexer_5_out), .sel(undriven_2));
  or or_1 (or_1_out, and_1_out, and_2_out);
  // Probe on instruction
  and and_1 (and_1_out, not_1_out, control_1_is_bne);
  and and_2 (and_2_out, alu_1_equal, control_1_is_beq);
  regfile regfile_1 (
    .rd(control_1_rd), .rt(control_1_rt), .rs(control_1_rs), .write_e(control_1_reg_we),
    .rd_data(multiplexer_5_out), .rs_data(regfile_1_rs_data), .rt_data(regfile_1_rt_data));
  not not_1 (not_1_out, alu_1_equal);
  Control control_1 (
    .Instruction(instruction), .rs(control_1_rs), .rd(control_1_rd), .rt(control_1_rt),
    .imm_sel(control_1_imm_sel), .imm(control_1_imm), .Reg_WE(control_1_reg_we),
    .ALU_code(control_1_alu_code), .ALU_MEMsel(control_1_alu_memsel), .we_mem(control_1_we_mem),
    .is_bne(control_1_is_bne), .is_beq(control_1_is_beq), .is_j(control_1_is_j));  // open: is_jal, is_jr, is_jalr
  Multiplexer #(.width(32)) multiplexer_6 (
    .in0(regfile_1_rs_data), .in1(regfile_1_rt_data), .out(multiplexer_6_out), .sel(or_3_out));
  assign bit_extender_5_out = {{16{multiplexer_8_out[15]}}, multiplexer_8_out};  // Bit_Extender bit_extender_5
  Shifter #(.shift("lr"), .width(16)) shifter_4 (.in(control_1_imm), .\dist (4'b0110), .out(shifter_4_out));
  Multiplexer #(.width(32)) multiplexer_7 (
    .in0(regfile_1_rt_data), .in1(bit_extender_5_out), .out(multiplexer_7_out), .sel(control_1_imm_sel));
  // OR_Gate or_2 is placed but not wired
  Multiplexer #(.width(16)) multiplexer_8 (
    .in0(control_1_imm), .in1(shifter_4_out), .out(multiplexer_8_out), .sel(or_3_out));
  Comparator #(.width(4)) comparator_1 (.a(control_1_alu_code), .b(4'b0110), .eq(comparator_1_eq));  // open: gt, lt
  Comparator #(.width(4)) comparator_2 (.a(control_1_alu_code), .b(4'b0111), .eq(comparator_2_eq));  // open: gt, lt
  ALU alu_1 (
    .ALU_CODE(control_1_alu_code), .OP1(multiplexer_6_out), .OP2(multiplexer_7_out), .equal(alu_1_equal),
    .Res(alu_1_res));
  or or_3 (or_3_out, comparator_1_eq, comparator_2_eq);
  Shifter #(.width(32)) shifter_5 (.in(alu_1_res), .\dist (5'b00010), .out(shifter_5_out));
  Bit_Extender #(.in_width(32)) bit_extender_6 (.in(shifter_5_out), .out(bit_extender_6_out));
  Clock clock_2 (.out(clock_2_out));
  RAM #(.addrWidth(16), .dataWidth(32), .enables("line")) ram_1 (
    .addr(bit_extender_6_out), .we(control_1_we_mem), .clk(clock_2_out), .din(regfile_1_rt_data),
    .dout(ram_1_dout));

  // Notes on the sheet:
  //   offset: word addressed
  //   PC + 4
  //   PC + 4 + Offset
  //   bne/beq
  //   jr/jalr
  //   any j*
  //   rs_data
  //   immediate
  //   label to jump to
  //   Tyeon Ford and Andy Quach
  //   ALU
  //   MEM
  //   PC + 4
  //   jal/jalr
  //   20080003
  //   00084900
  //   ----
  //   res value from ALU
  //   value from memory
  //   only write enable if the instruction should
  //   beq == 1 if the two registers are equal
  //   data from specified rs register
  //   data from specified rt register
  //   bne =/= 1 if the two registers are NOT equal
  //   rd register
  //   rt register
  //   use imm?
  //   rs register
  //   only =1 if it is operating with an imm, otherwise operate with rt_data
  //   only if sll or srl
  //   move shamt
  //   from 10:6 to 3:0 
  //   sll
  //   srl
endmodule

module regfile (
  input  [31:0] rd_data,
  input  write_e,
  input  [4:0] rs,
  input  [4:0] rd,
  input  [4:0] rt,
  output [31:0] rs_data,
  output [31:0] rt_data
);

  wire and_1_out, and_2_out, and_3_out, and_4_out, and_5_out, and_6_out, and_7_out, and_8_out, and_9_out,
       and_10_out, and_11_out, and_12_out, and_13_out, and_14_out, and_15_out, and_16_out, and_17_out,
       and_18_out, and_19_out, and_20_out, and_21_out, and_22_out, and_23_out, and_24_out, and_25_out,
       and_26_out, and_27_out, and_28_out, and_29_out, and_30_out, and_31_out, clock_1_out,
       demultiplexer_1_out1, demultiplexer_1_out2, demultiplexer_1_out3, demultiplexer_1_out4,
       demultiplexer_1_out5, demultiplexer_1_out6, demultiplexer_1_out7, demultiplexer_1_out8,
       demultiplexer_1_out9, demultiplexer_1_out10, demultiplexer_1_out11, demultiplexer_1_out12,
       demultiplexer_1_out13, demultiplexer_1_out14, demultiplexer_1_out15, demultiplexer_1_out16,
       demultiplexer_1_out17, demultiplexer_1_out18, demultiplexer_1_out19, demultiplexer_1_out20,
       demultiplexer_1_out21, demultiplexer_1_out22, demultiplexer_1_out23, demultiplexer_1_out24,
       demultiplexer_1_out25, demultiplexer_1_out26, demultiplexer_1_out27, demultiplexer_1_out28,
       demultiplexer_1_out29, demultiplexer_1_out30, demultiplexer_1_out31;
  wire [31:0] register_1_q, register_2_q, register_3_q, register_4_q, register_5_q, register_6_q,
       register_7_q, register_8_q, register_9_q, register_10_q, register_11_q, register_12_q, register_13_q,
       register_14_q, register_15_q, register_16_q, register_17_q, register_18_q, register_19_q,
       register_20_q, register_21_q, register_22_q, register_23_q, register_24_q, register_25_q,
       register_26_q, register_27_q, register_28_q, register_29_q, register_30_q, register_31_q;

  Demultiplexer #(.select(5)) demultiplexer_1 (
    .out1(demultiplexer_1_out1), .out2(demultiplexer_1_out2), .out3(demultiplexer_1_out3),
    .out4(demultiplexer_1_out4), .out5(demultiplexer_1_out5), .out6(demultiplexer_1_out6),
    .out7(demultiplexer_1_out7), .out8(demultiplexer_1_out8), .out9(demultiplexer_1_out9),
    .out10(demultiplexer_1_out10), .out11(demultiplexer_1_out11), .out12(demultiplexer_1_out12),
    .out13(demultiplexer_1_out13), .out14(demultiplexer_1_out14), .out15(demultiplexer_1_out15),
    .out16(demultiplexer_1_out16), .out17(demultiplexer_1_out17), .out18(demultiplexer_1_out18),
    .out19(demultiplexer_1_out19), .out20(demultiplexer_1_out20), .out21(demultiplexer_1_out21),
    .out22(demultiplexer_1_out22), .out23(demultiplexer_1_out23), .out24(demultiplexer_1_out24),
    .out25(demultiplexer_1_out25), .out26(demultiplexer_1_out26), .out27(demultiplexer_1_out27),
    .out28(demultiplexer_1_out28), .out29(demultiplexer_1_out29), .out30(demultiplexer_1_out30),
    .out31(demultiplexer_1_out31), .in(1'b1), .sel(rd));  // open: out0
  Clock clock_1 (.out(clock_1_out));
  and and_1 (and_1_out, write_e, demultiplexer_1_out1);
  and and_2 (and_2_out, write_e, demultiplexer_1_out5);
  and and_3 (and_3_out, write_e, demultiplexer_1_out9);
  and and_4 (and_4_out, write_e, demultiplexer_1_out13);
  and and_5 (and_5_out, write_e, demultiplexer_1_out17);
  and and_6 (and_6_out, write_e, demultiplexer_1_out21);
  and and_7 (and_7_out, write_e, demultiplexer_1_out25);
  and and_8 (and_8_out, write_e, demultiplexer_1_out29);
  Register #(.width(32)) register_1 (.D(rd_data), .en(and_1_out), .clk(clock_1_out), .Q(register_1_q));  // open: clr
  Register #(.width(32)) register_2 (.D(rd_data), .en(and_2_out), .clk(clock_1_out), .Q(register_2_q));  // open: clr
  Register #(.width(32)) register_3 (.D(rd_data), .en(and_3_out), .clk(clock_1_out), .Q(register_3_q));  // open: clr
  Register #(.width(32)) register_4 (.D(rd_data), .en(and_4_out), .clk(clock_1_out), .Q(register_4_q));  // open: clr
  Register #(.width(32)) register_5 (.D(rd_data), .en(and_5_out), .clk(clock_1_out), .Q(register_5_q));  // open: clr
  Register #(.width(32)) register_6 (.D(rd_data), .en(and_6_out), .clk(clock_1_out), .Q(register_6_q));  // open: clr
  Register #(.width(32)) register_7 (.D(rd_data), .en(and_7_out), .clk(clock_1_out), .Q(register_7_q));  // open: clr
  Register #(.width(32)) register_8 (.D(rd_data), .en(and_8_out), .clk(clock_1_out), .Q(register_8_q));  // open: clr
  and and_9 (and_9_out, write_e, demultiplexer_1_out2);
  and and_10 (and_10_out, write_e, demultiplexer_1_out6);
  and and_11 (and_11_out, write_e, demultiplexer_1_out10);
  and and_12 (and_12_out, write_e, demultiplexer_1_out14);
  and and_13 (and_13_out, write_e, demultiplexer_1_out18);
  and and_14 (and_14_out, write_e, demultiplexer_1_out22);
  and and_15 (and_15_out, write_e, demultiplexer_1_out26);
  and and_16 (and_16_out, write_e, demultiplexer_1_out30);
  Register #(.width(32)) register_9 (.D(rd_data), .en(and_9_out), .clk(clock_1_out), .Q(register_9_q));  // open: clr
  Register #(.width(32)) register_10 (.D(rd_data), .en(and_10_out), .clk(clock_1_out), .Q(register_10_q));  // open: clr
  Register #(.width(32)) register_11 (.D(rd_data), .en(and_11_out), .clk(clock_1_out), .Q(register_11_q));  // open: clr
  Register #(.width(32)) register_12 (.D(rd_data), .en(and_12_out), .clk(clock_1_out), .Q(register_12_q));  // open: clr
  Register #(.width(32)) register_13 (.D(rd_data), .en(and_13_out), .clk(clock_1_out), .Q(register_13_q));  // open: clr
  Register #(.width(32)) register_14 (.D(rd_data), .en(and_14_out), .clk(clock_1_out), .Q(register_14_q));  // open: clr
  Register #(.width(32)) register_15 (.D(rd_data), .en(and_15_out), .clk(clock_1_out), .Q(register_15_q));  // open: clr
  Register #(.width(32)) register_16 (.D(rd_data), .en(and_16_out), .clk(clock_1_out), .Q(register_16_q));  // open: clr
  and and_17 (and_17_out, write_e, demultiplexer_1_out3);
  and and_18 (and_18_out, write_e, demultiplexer_1_out7);
  and and_19 (and_19_out, write_e, demultiplexer_1_out11);
  and and_20 (and_20_out, write_e, demultiplexer_1_out15);
  and and_21 (and_21_out, write_e, demultiplexer_1_out19);
  and and_22 (and_22_out, write_e, demultiplexer_1_out23);
  and and_23 (and_23_out, write_e, demultiplexer_1_out27);
  and and_24 (and_24_out, write_e, demultiplexer_1_out31);
  Register #(.width(32)) register_17 (.D(rd_data), .en(and_17_out), .clk(clock_1_out), .Q(register_17_q));  // open: clr
  Register #(.width(32)) register_18 (.D(rd_data), .en(and_18_out), .clk(clock_1_out), .Q(register_18_q));  // open: clr
  Register #(.width(32)) register_19 (.D(rd_data), .en(and_19_out), .clk(clock_1_out), .Q(register_19_q));  // open: clr
  Register #(.width(32)) register_20 (.D(rd_data), .en(and_20_out), .clk(clock_1_out), .Q(register_20_q));  // open: clr
  Register #(.width(32)) register_21 (.D(rd_data), .en(and_21_out), .clk(clock_1_out), .Q(register_21_q));  // open: clr
  Register #(.width(32)) register_22 (.D(rd_data), .en(and_22_out), .clk(clock_1_out), .Q(register_22_q));  // open: clr
  Register #(.width(32)) register_23 (.D(rd_data), .en(and_23_out), .clk(clock_1_out), .Q(register_23_q));  // open: clr
  Register #(.width(32)) register_24 (.D(rd_data), .en(and_24_out), .clk(clock_1_out), .Q(register_24_q));  // open: clr
  Register #(.width(32)) register_25 (.D(rd_data), .en(and_25_out), .clk(clock_1_out), .Q(register_25_q));  // open: clr
  and and_25 (and_25_out, write_e, demultiplexer_1_out4);
  Register #(.width(32)) register_26 (.D(rd_data), .en(and_26_out), .clk(clock_1_out), .Q(register_26_q));  // open: clr
  and and_26 (and_26_out, write_e, demultiplexer_1_out8);
  Register #(.width(32)) register_27 (.D(rd_data), .en(and_27_out), .clk(clock_1_out), .Q(register_27_q));  // open: clr
  and and_27 (and_27_out, write_e, demultiplexer_1_out12);
  Register #(.width(32)) register_28 (.D(rd_data), .en(and_28_out), .clk(clock_1_out), .Q(register_28_q));  // open: clr
  and and_28 (and_28_out, write_e, demultiplexer_1_out16);
  Register #(.width(32)) register_29 (.D(rd_data), .en(and_29_out), .clk(clock_1_out), .Q(register_29_q));  // open: clr
  and and_29 (and_29_out, write_e, demultiplexer_1_out20);
  Register #(.width(32)) register_30 (.D(rd_data), .en(and_30_out), .clk(clock_1_out), .Q(register_30_q));  // open: clr
  and and_30 (and_30_out, write_e, demultiplexer_1_out24);
  Register #(.width(32)) register_31 (.D(rd_data), .en(and_31_out), .clk(clock_1_out), .Q(register_31_q));  // open: clr
  and and_31 (and_31_out, write_e, demultiplexer_1_out28);
  Multiplexer #(.select(5), .width(32)) multiplexer_1 (
    .in0({32{1'b0}}), .in1(register_1_q), .in2(register_9_q), .in3(register_17_q), .in4(register_25_q),
    .in5(register_2_q), .in6(register_10_q), .in7(register_18_q), .in8(register_26_q), .in9(register_3_q),
    .in10(register_11_q), .in11(register_19_q), .in12(register_27_q), .in13(register_4_q),
    .in14(register_12_q), .in15(register_20_q), .in16(register_28_q), .in17(register_5_q),
    .in18(register_13_q), .in19(register_21_q), .in20(register_29_q), .in21(register_6_q),
    .in22(register_14_q), .in23(register_22_q), .in24(register_30_q), .in25(register_7_q),
    .in26(register_15_q), .in27(register_23_q), .in28(register_31_q), .in29(register_8_q),
    .in30(register_16_q), .in31(register_24_q), .out(rs_data), .sel(rs));
  Multiplexer #(.select(5), .width(32)) multiplexer_2 (
    .in1(register_1_q), .in2(register_9_q), .in3(register_17_q), .in4(register_25_q), .in5(register_2_q),
    .in6(register_10_q), .in7(register_18_q), .in8(register_26_q), .in9(register_3_q), .in10(register_11_q),
    .in11(register_19_q), .in12(register_27_q), .in13(register_4_q), .in14(register_12_q),
    .in15(register_20_q), .in16(register_28_q), .in17(register_5_q), .in18(register_13_q),
    .in19(register_21_q), .in20(register_29_q), .in21(register_6_q), .in22(register_14_q),
    .in23(register_22_q), .in24(register_30_q), .in25(register_7_q), .in26(register_15_q),
    .in27(register_23_q), .in28(register_31_q), .in29(register_8_q), .in30(register_16_q),
    .in31(register_24_q), .out(rt_data), .sel(rt));  // open: in0

  // Notes on the sheet:
  //   Tyeon Ford and Andy Quach
  //   (can't write to zero register since it should be constant)
  //   To decide which register to write data to
  //   Will only write to a register if the instruction should at all
  //   and if that register is specifically chosen
  //   The data that will be written to a register
  //   $at
  //   $a1
  //   $t1
  //   $v0
  //   $a2
  //   $t2
  //   $v1
  //   $a3
  //   $a0
  //   $t0
  //   zero register should always output 0
  //   Reads the data from a specific source register
  //   Reads the data from a specific register
endmodule

module ALU (
  input  [3:0] ALU_CODE,
  input  [31:0] OP1,
  input  [31:0] OP2,
  output [31:0] Res,
  output equal
);

  wire clock_1_out, comparator_1_lt, comparator_3_eq, comparator_4_eq, or_2_out;
  wire [4:0] bit_extender_1_out, bit_extender_2_out;
  wire [31:0] adder_1_out, and_1_out, bit_extender_3_out, divider_1_out, divider_1_rem, HI_q, LO_q,
       multiplexer_1_out, multiplexer_2_out, multiplier_1_cout, multiplier_1_out, nor_1_out, or_1_out,
       shifter_1_out, shifter_2_out, shifter_3_out, subtractor_1_out, xor_1_out;

  Clock clock_1 (.out(clock_1_out));
  Bit_Extender #(.in_width(32), .out_width(5), .\type ("zero")) bit_extender_1 (.in(OP2), .out(bit_extender_1_out));
  Bit_Extender #(.in_width(32), .out_width(5), .\type ("zero")) bit_extender_2 (.in(OP2), .out(bit_extender_2_out));
  Adder #(.width(32)) adder_1 (.a(OP1), .b(OP2), .out(adder_1_out));  // open: cin, cout
  Subtractor #(.width(32)) subtractor_1 (.a(OP1), .b(OP2), .out(subtractor_1_out));  // open: bin, bout
  Shifter #(.width(32)) shifter_1 (.in(OP1), .\dist (bit_extender_1_out), .out(shifter_1_out));
  Shifter #(.shift("lr"), .width(32)) shifter_2 (.in(OP1), .\dist (bit_extender_2_out), .out(shifter_2_out));
  Comparator #(.width(32)) comparator_1 (.a(OP1), .b(OP2), .lt(comparator_1_lt));  // open: gt, eq
  assign and_1_out = OP1 & OP2;  // AND_Gate and_1, 32 bits wide
  assign or_1_out = OP1 | OP2;  // OR_Gate or_1, 32 bits wide
  assign nor_1_out = ~(OP1 | OP2);  // NOR_Gate nor_1, 32 bits wide
  assign xor_1_out = OP1 ^ OP2;  // XOR_Gate xor_1, 32 bits wide
  Shifter #(.width(32)) shifter_3 (.in(OP1), .\dist (5'b10000), .out(shifter_3_out));
  Comparator #(.width(32)) comparator_2 (.a(OP1), .b(OP2), .eq(equal));  // open: gt, lt
  Multiplier #(.width(32)) multiplier_1 (
    .a(OP1), .b(OP2), .out(multiplier_1_out), .cout(multiplier_1_cout));  // open: cin
  Divider #(.width(32)) divider_1 (.a(OP1), .b(OP2), .out(divider_1_out), .rem(divider_1_rem));  // open: upper
  assign bit_extender_3_out = {{31{1'b0}}, comparator_1_lt};  // Bit_Extender bit_extender_3
  Multiplexer #(.width(32)) multiplexer_1 (
    .in0(multiplier_1_out), .in1(divider_1_out), .out(multiplexer_1_out), .sel(comparator_4_eq));
  Multiplexer #(.width(32)) multiplexer_2 (
    .in0(multiplier_1_cout), .in1(divider_1_rem), .out(multiplexer_2_out), .sel(comparator_4_eq));
  Comparator #(.width(4)) comparator_3 (.a(ALU_CODE), .b(4'b0010), .eq(comparator_3_eq));  // open: gt, lt
  Comparator #(.width(4)) comparator_4 (.a(ALU_CODE), .b(4'b0011), .eq(comparator_4_eq));  // open: gt, lt
  or or_2 (or_2_out, comparator_3_eq, comparator_4_eq);
  Register #(.width(32)) LO (.D(multiplexer_1_out), .en(or_2_out), .clk(clock_1_out), .Q(LO_q));  // open: clr
  Register #(.width(32)) HI (.D(multiplexer_2_out), .en(or_2_out), .clk(clock_1_out), .Q(HI_q));  // open: clr
  Multiplexer #(.select(4), .width(32)) multiplexer_3 (
    .in0(adder_1_out), .in1(subtractor_1_out), .in4(LO_q), .in5(HI_q), .in6(shifter_1_out),
    .in7(shifter_2_out), .in8(bit_extender_3_out), .in9(and_1_out), .in10(or_1_out), .in11(nor_1_out),
    .in12(xor_1_out), .in13(shifter_3_out), .out(Res), .sel(ALU_CODE));  // open: in2, in3, in14, in15

  // Notes on the sheet:
  //   Andy Quach and Tyeon Ford
  //   add/addi
  //   subtract
  //   sll
  //   srl
  //   AND
  //   OR
  //   LUI
  //   slt
  //   NOR
  //   XOR
  //   Product
  //   Overflow
  //   Quotient
  //   Remainder
endmodule

module Control (
  input  [31:0] Instruction,
  output [4:0] rs,
  output [4:0] rd,
  output [4:0] rt,
  output imm_sel,
  output [15:0] imm,
  output Reg_WE,
  output [3:0] ALU_code,
  output ALU_MEMsel,
  output we_mem,
  output is_bne,
  output is_beq,
  output is_j,
  output is_jal,
  output is_jr,
  output is_jalr
);

  wire and_1_out, and_2_out, comparator_1_eq, comparator_2_eq, comparator_3_eq, comparator_4_eq,
       comparator_5_eq, comparator_6_eq, comparator_7_eq, comparator_8_eq, comparator_9_eq, comparator_10_eq,
       comparator_11_eq, comparator_12_eq, comparator_13_eq, comparator_14_eq, comparator_15_eq,
       comparator_16_eq, comparator_17_eq, comparator_18_eq, comparator_19_eq, comparator_28_eq,
       comparator_29_eq, not_1_out, not_2_out, not_3_out, or_2_out, or_3_out, or_4_out, or_6_out, or_8_out,
       or_9_out;
  wire [3:0] adder_1_out, adder_2_out, adder_3_out, adder_4_out, adder_5_out, adder_6_out, adder_7_out,
       adder_8_out, adder_9_out, adder_10_out, adder_11_out, adder_12_out, adder_13_out, adder_14_out,
       adder_15_out, adder_16_out, adder_17_out, adder_18_out, adder_19_out, adder_20_out, adder_21_out,
       adder_22_out, demultiplexer_5_out0, demultiplexer_5_out1, demultiplexer_6_out0, demultiplexer_6_out1,
       demultiplexer_7_out0, demultiplexer_7_out1, demultiplexer_8_out0, demultiplexer_8_out1,
       demultiplexer_9_out0, demultiplexer_9_out1, demultiplexer_10_out0, demultiplexer_10_out1,
       demultiplexer_11_out0, demultiplexer_11_out1, demultiplexer_12_out0, demultiplexer_12_out1,
       demultiplexer_13_out0, demultiplexer_13_out1, demultiplexer_14_out0, demultiplexer_14_out1,
       demultiplexer_15_out0, demultiplexer_15_out1, demultiplexer_16_out0, demultiplexer_16_out1,
       demultiplexer_17_out0, demultiplexer_17_out1, demultiplexer_18_out0, demultiplexer_18_out1,
       demultiplexer_19_out0, demultiplexer_19_out1, demultiplexer_20_out0, demultiplexer_20_out1,
       demultiplexer_21_out0, demultiplexer_21_out1, demultiplexer_22_out0, demultiplexer_22_out1,
       demultiplexer_23_out0, demultiplexer_23_out1, demultiplexer_24_out0, demultiplexer_24_out1,
       demultiplexer_25_out0, demultiplexer_25_out1, demultiplexer_26_out0, demultiplexer_26_out1,
       multiplexer_2_out, multiplexer_3_out, multiplexer_4_out, multiplexer_5_out, multiplexer_6_out,
       multiplexer_7_out, multiplexer_8_out, multiplexer_9_out, multiplexer_10_out, multiplexer_11_out,
       multiplexer_12_out, multiplexer_13_out, multiplexer_14_out, multiplexer_15_out, or_7_out, undriven,
       undriven_2;
  wire [4:0] demultiplexer_1_out0, demultiplexer_2_out1, demultiplexer_3_out0, demultiplexer_3_out1;
  wire [5:0] demultiplexer_4_out1;

  Comparator #(.mode("unsigned"), .width(6)) comparator_1 (
    .a({6{1'b0}}), .b(Instruction[31:26]), .eq(comparator_1_eq));  // open: gt, lt
  Comparator #(.width(1)) comparator_2 (.a(1'b0), .b(comparator_1_eq), .eq(comparator_2_eq));  // open: gt, lt
  Demultiplexer #(.width(5)) demultiplexer_1 (
    .out0(demultiplexer_1_out0), .out1(rt), .in(Instruction[20:16]), .sel(comparator_1_eq));
  Demultiplexer #(.width(5)) demultiplexer_2 (
    .out0(imm[15:11]), .out1(demultiplexer_2_out1), .in(Instruction[15:11]), .sel(comparator_1_eq));
  Demultiplexer #(.width(5)) demultiplexer_3 (
    .out0(demultiplexer_3_out0), .out1(demultiplexer_3_out1), .in(Instruction[10:6]), .sel(comparator_1_eq));
  Demultiplexer #(.width(6)) demultiplexer_4 (
    .out0(imm[5:0]), .out1(demultiplexer_4_out1), .in(Instruction[5:0]), .sel(comparator_1_eq));
  assign imm[10:6] = demultiplexer_3_out0 | demultiplexer_3_out1;  // OR_Gate or_1, 5 bits wide
  not not_1 (not_1_out, comparator_2_eq);
  Comparator #(.width(6)) comparator_3 (.a(6'b100000), .b(demultiplexer_4_out1), .eq(comparator_3_eq));  // open: gt, lt
  Comparator #(.width(6)) comparator_4 (.a(6'b100010), .b(demultiplexer_4_out1), .eq(comparator_4_eq));  // open: gt, lt
  Comparator #(.width(6)) comparator_5 (.a(6'b011000), .b(demultiplexer_4_out1), .eq(comparator_5_eq));  // open: gt, lt
  Comparator #(.width(6)) comparator_6 (.a(6'b011010), .b(demultiplexer_4_out1), .eq(comparator_6_eq));  // open: gt, lt
  Comparator #(.width(6)) comparator_7 (.a(6'b010010), .b(demultiplexer_4_out1), .eq(comparator_7_eq));  // open: gt, lt
  Comparator #(.width(6)) comparator_8 (.a(6'b010000), .b(demultiplexer_4_out1), .eq(comparator_8_eq));  // open: gt, lt
  Comparator #(.width(6)) comparator_9 (.a({6{1'b0}}), .b(demultiplexer_4_out1), .eq(comparator_9_eq));  // open: gt, lt
  and and_1 (and_1_out, comparator_9_eq, not_1_out);
  Comparator #(.width(6)) comparator_10 (
    .a(6'b000010), .b(demultiplexer_4_out1), .eq(comparator_10_eq));  // open: gt, lt
  Comparator #(.width(6)) comparator_11 (
    .a(6'b101010), .b(demultiplexer_4_out1), .eq(comparator_11_eq));  // open: gt, lt
  Comparator #(.width(6)) comparator_12 (
    .a(6'b100100), .b(demultiplexer_4_out1), .eq(comparator_12_eq));  // open: gt, lt
  or or_2 (or_2_out, comparator_12_eq, comparator_13_eq);
  Comparator #(.width(6)) comparator_13 (.a(6'b001100), .b(Instruction[31:26]), .eq(comparator_13_eq));  // open: gt, lt
  Comparator #(.width(6)) comparator_14 (
    .a(6'b100101), .b(demultiplexer_4_out1), .eq(comparator_14_eq));  // open: gt, lt
  Comparator #(.width(6)) comparator_15 (.a(6'b001101), .b(Instruction[31:26]), .eq(comparator_15_eq));  // open: gt, lt
  Comparator #(.width(6)) comparator_16 (
    .a(6'b100110), .b(demultiplexer_4_out1), .eq(comparator_16_eq));  // open: gt, lt
  Comparator #(.width(6)) comparator_17 (.a(6'b001110), .b(Instruction[31:26]), .eq(comparator_17_eq));  // open: gt, lt
  Comparator #(.width(6)) comparator_18 (
    .a(6'b100111), .b(demultiplexer_4_out1), .eq(comparator_18_eq));  // open: gt, lt
  Comparator #(.width(6)) comparator_19 (
    .a(6'b001111), .b(demultiplexer_4_out1), .eq(comparator_19_eq));  // open: gt, lt
  Comparator #(.width(6)) comparator_20 (.a(6'b100011), .b(Instruction[31:26]), .eq(ALU_MEMsel));  // open: gt, lt
  Comparator #(.width(6)) comparator_21 (.a(6'b101011), .b(Instruction[31:26]), .eq(we_mem));  // open: gt, lt
  Comparator #(.width(6)) comparator_22 (.a(6'b000101), .b(Instruction[31:26]), .eq(is_bne));  // open: gt, lt
  Comparator #(.width(6)) comparator_23 (.a(6'b000100), .b(Instruction[31:26]), .eq(is_beq));  // open: gt, lt
  Comparator #(.width(6)) comparator_24 (.a(6'b000010), .b(Instruction[31:26]), .eq(is_j));  // open: gt, lt
  Comparator #(.width(6)) comparator_25 (.a(6'b000011), .b(Instruction[31:26]), .eq(is_jal));  // open: gt, lt
  Comparator #(.width(6)) comparator_26 (.a(6'b000011), .b(demultiplexer_4_out1), .eq(is_jr));  // open: gt, lt
  Comparator #(.width(6)) comparator_27 (.a(6'b000011), .b(demultiplexer_4_out1), .eq(is_jalr));  // open: gt, lt
  not not_2 (not_2_out, comparator_1_eq);
  Demultiplexer #(.width(4)) demultiplexer_5 (
    .out0(demultiplexer_5_out0), .out1(demultiplexer_5_out1), .in(4'b0000), .sel(comparator_3_eq));
  Demultiplexer #(.width(4)) demultiplexer_6 (
    .out0(demultiplexer_6_out0), .out1(demultiplexer_6_out1), .in(adder_1_out), .sel(comparator_4_eq));
  Demultiplexer #(.width(4)) demultiplexer_7 (
    .out0(demultiplexer_7_out0), .out1(demultiplexer_7_out1), .in(adder_2_out), .sel(comparator_5_eq));
  Demultiplexer #(.width(4)) demultiplexer_8 (
    .out0(demultiplexer_8_out0), .out1(demultiplexer_8_out1), .in(adder_3_out), .sel(comparator_6_eq));
  Demultiplexer #(.width(4)) demultiplexer_9 (
    .out0(demultiplexer_9_out0), .out1(demultiplexer_9_out1), .in(adder_4_out), .sel(comparator_7_eq));
  Demultiplexer #(.width(4)) demultiplexer_10 (
    .out0(demultiplexer_10_out0), .out1(demultiplexer_10_out1), .in(adder_5_out), .sel(comparator_8_eq));
  Demultiplexer #(.width(4)) demultiplexer_11 (
    .out0(demultiplexer_11_out0), .out1(demultiplexer_11_out1), .in(adder_6_out), .sel(and_1_out));
  Demultiplexer #(.width(4)) demultiplexer_12 (
    .out0(demultiplexer_12_out0), .out1(demultiplexer_12_out1), .in(adder_7_out), .sel(comparator_10_eq));
  Demultiplexer #(.width(4)) demultiplexer_13 (
    .out0(demultiplexer_13_out0), .out1(demultiplexer_13_out1), .in(adder_8_out), .sel(comparator_11_eq));
  Demultiplexer #(.width(4)) demultiplexer_14 (
    .out0(demultiplexer_14_out0), .out1(demultiplexer_14_out1), .in(adder_9_out), .sel(or_2_out));
  Demultiplexer #(.width(4)) demultiplexer_15 (
    .out0(demultiplexer_15_out0), .out1(demultiplexer_15_out1), .in(adder_10_out), .sel(or_3_out));
  or or_3 (or_3_out, comparator_14_eq, comparator_15_eq);
  Demultiplexer #(.width(4)) demultiplexer_16 (
    .out0(demultiplexer_16_out0), .out1(demultiplexer_16_out1), .in(adder_11_out), .sel(or_4_out));
  or or_4 (or_4_out, comparator_16_eq, comparator_17_eq);
  Demultiplexer #(.width(4)) demultiplexer_17 (
    .out0(demultiplexer_17_out0), .out1(demultiplexer_17_out1), .in(adder_12_out), .sel(comparator_18_eq));
  Demultiplexer #(.width(4)) demultiplexer_18 (
    .out0(demultiplexer_18_out0), .out1(demultiplexer_18_out1), .in(adder_13_out), .sel(comparator_19_eq));
  Demultiplexer #(.width(4)) demultiplexer_19 (
    .out0(demultiplexer_19_out0), .out1(demultiplexer_19_out1), .in(adder_14_out), .sel(ALU_MEMsel));
  Demultiplexer #(.width(4)) demultiplexer_20 (
    .out0(demultiplexer_20_out0), .out1(demultiplexer_20_out1), .in(adder_15_out), .sel(we_mem));
  Demultiplexer #(.width(4)) demultiplexer_21 (
    .out0(demultiplexer_21_out0), .out1(demultiplexer_21_out1), .in(adder_16_out), .sel(is_bne));
  Demultiplexer #(.width(4)) demultiplexer_22 (
    .out0(demultiplexer_22_out0), .out1(demultiplexer_22_out1), .in(adder_17_out), .sel(is_beq));
  Demultiplexer #(.width(4)) demultiplexer_23 (
    .out0(demultiplexer_23_out0), .out1(demultiplexer_23_out1), .in(adder_18_out), .sel(is_j));
  Demultiplexer #(.width(4)) demultiplexer_24 (
    .out0(demultiplexer_24_out0), .out1(demultiplexer_24_out1), .in(adder_19_out), .sel(is_jal));
  Demultiplexer #(.width(4)) demultiplexer_25 (
    .out0(demultiplexer_25_out0), .out1(demultiplexer_25_out1), .in(undriven), .sel(is_jr));
  Demultiplexer #(.width(4)) demultiplexer_26 (
    .out0(demultiplexer_26_out0), .out1(demultiplexer_26_out1), .in(undriven_2), .sel(is_jalr));
  Adder #(.width(4)) adder_1 (.a(demultiplexer_5_out0), .b(4'b0001), .out(adder_1_out));  // open: cin, cout
  Adder #(.width(4)) adder_2 (.a(demultiplexer_6_out0), .b(4'b0001), .out(adder_2_out));  // open: cin, cout
  Adder #(.width(4)) adder_3 (.a(demultiplexer_7_out0), .b(4'b0001), .out(adder_3_out));  // open: cin, cout
  Adder #(.width(4)) adder_4 (.a(demultiplexer_8_out0), .b(4'b0001), .out(adder_4_out));  // open: cin, cout
  Adder #(.width(4)) adder_5 (.a(demultiplexer_9_out0), .b(4'b0001), .out(adder_5_out));  // open: cin, cout
  Adder #(.width(4)) adder_6 (.a(demultiplexer_10_out0), .b(4'b0001), .out(adder_6_out));  // open: cin, cout
  Adder #(.width(4)) adder_7 (.a(demultiplexer_11_out0), .b(4'b0001), .out(adder_7_out));  // open: cin, cout
  Adder #(.width(4)) adder_8 (.a(demultiplexer_12_out0), .b(4'b0001), .out(adder_8_out));  // open: cin, cout
  Adder #(.width(4)) adder_9 (.a(demultiplexer_13_out0), .b(4'b0001), .out(adder_9_out));  // open: cin, cout
  Adder #(.width(4)) adder_10 (.a(demultiplexer_14_out0), .b(4'b0001), .out(adder_10_out));  // open: cin, cout
  Adder #(.width(4)) adder_11 (.a(demultiplexer_15_out0), .b(4'b0001), .out(adder_11_out));  // open: cin, cout
  Adder #(.width(4)) adder_12 (.a(demultiplexer_16_out0), .b(4'b0001), .out(adder_12_out));  // open: cin, cout
  Adder #(.width(4)) adder_13 (.a(demultiplexer_17_out0), .b(4'b0001), .out(adder_13_out));  // open: cin, cout
  Adder #(.width(4)) adder_14 (.a(demultiplexer_18_out0), .b(4'b0001), .out(adder_14_out));  // open: cin, cout
  Adder #(.width(4)) adder_15 (.a(demultiplexer_19_out0), .b(4'b0001), .out(adder_15_out));  // open: cin, cout
  Adder #(.width(4)) adder_16 (.a(demultiplexer_20_out0), .b(4'b0001), .out(adder_16_out));  // open: cin, cout
  Adder #(.width(4)) adder_17 (.a(demultiplexer_21_out0), .b(4'b0001), .out(adder_17_out));  // open: cin, cout
  Adder #(.width(4)) adder_18 (.a(demultiplexer_22_out0), .b(4'b0001), .out(adder_18_out));  // open: cin, cout
  Adder #(.width(4)) adder_19 (.a(demultiplexer_23_out0), .b(4'b0001), .out(adder_19_out));  // open: cin, cout
  Adder #(.width(4)) adder_20 (.a(demultiplexer_24_out0), .b(4'b0001), .out(adder_20_out));  // open: cin, cout
  Adder #(.width(4)) adder_21 (.a(demultiplexer_25_out0), .b(4'b0001), .out(adder_21_out));  // open: cin, cout
  Adder #(.width(4)) adder_22 (.a(demultiplexer_26_out0), .b(4'b0001), .out(adder_22_out));  // open: cin, cout
  Multiplexer #(.width(5)) multiplexer_1 (
    .in0(demultiplexer_1_out0), .in1(demultiplexer_2_out1), .out(rd), .sel(comparator_1_eq));
  or or_5 (imm_sel, not_2_out, or_6_out);
  Multiplexer #(.width(4)) multiplexer_2 (
    .in0(4'b0000), .in1(demultiplexer_5_out1), .out(multiplexer_2_out), .sel(comparator_3_eq));
  Multiplexer #(.width(4)) multiplexer_3 (
    .in0(4'b0000), .in1(demultiplexer_6_out1), .out(multiplexer_3_out), .sel(comparator_4_eq));
  Multiplexer #(.width(4)) multiplexer_4 (
    .in0(4'b0000), .in1(demultiplexer_7_out1), .out(multiplexer_4_out), .sel(comparator_5_eq));
  Multiplexer #(.width(4)) multiplexer_5 (
    .in0(4'b0000), .in1(demultiplexer_8_out1), .out(multiplexer_5_out), .sel(comparator_6_eq));
  Multiplexer #(.width(4)) multiplexer_6 (
    .in0(4'b0000), .in1(demultiplexer_9_out1), .out(multiplexer_6_out), .sel(comparator_7_eq));
  Multiplexer #(.width(4)) multiplexer_7 (
    .in0(4'b0000), .in1(demultiplexer_10_out1), .out(multiplexer_7_out), .sel(comparator_8_eq));
  Multiplexer #(.width(4)) multiplexer_8 (
    .in0(4'b0000), .in1(demultiplexer_11_out1), .out(multiplexer_8_out), .sel(and_1_out));
  Multiplexer #(.width(4)) multiplexer_9 (
    .in0(4'b0000), .in1(demultiplexer_12_out1), .out(multiplexer_9_out), .sel(comparator_10_eq));
  Multiplexer #(.width(4)) multiplexer_10 (
    .in0(4'b0000), .in1(demultiplexer_13_out1), .out(multiplexer_10_out), .sel(comparator_11_eq));
  Multiplexer #(.width(4)) multiplexer_11 (
    .in0(4'b0000), .in1(demultiplexer_14_out1), .out(multiplexer_11_out), .sel(or_2_out));
  Multiplexer #(.width(4)) multiplexer_12 (
    .in0(4'b0000), .in1(demultiplexer_15_out1), .out(multiplexer_12_out), .sel(or_3_out));
  Multiplexer #(.width(4)) multiplexer_13 (
    .in0(4'b0000), .in1(demultiplexer_16_out1), .out(multiplexer_13_out), .sel(or_4_out));
  Multiplexer #(.width(4)) multiplexer_14 (
    .in0(4'b0000), .in1(demultiplexer_17_out1), .out(multiplexer_14_out), .sel(comparator_18_eq));
  Multiplexer #(.width(4)) multiplexer_15 (
    .in0(4'b0000), .in1(demultiplexer_18_out1), .out(multiplexer_15_out), .sel(comparator_19_eq));
  Multiplexer #(.width(4)) multiplexer_16 (.in0(4'b0000), .in1(demultiplexer_19_out1), .sel(ALU_MEMsel));  // open: out
  Multiplexer #(.width(4)) multiplexer_17 (.in0(4'b0000), .in1(demultiplexer_20_out1), .sel(we_mem));  // open: out
  Multiplexer #(.width(4)) multiplexer_18 (.in0(4'b0000), .in1(demultiplexer_21_out1), .sel(is_bne));  // open: out
  Multiplexer #(.width(4)) multiplexer_19 (.in0(4'b0000), .in1(demultiplexer_22_out1), .sel(is_beq));  // open: out
  Multiplexer #(.width(4)) multiplexer_20 (.in0(4'b0000), .in1(demultiplexer_23_out1), .sel(is_j));  // open: out
  Multiplexer #(.width(4)) multiplexer_21 (.in0(4'b0000), .in1(demultiplexer_24_out1), .sel(is_jal));  // open: out
  Multiplexer #(.width(4)) multiplexer_22 (.in0(4'b0000), .in1(demultiplexer_25_out1), .sel(is_jr));  // open: out
  Multiplexer #(.width(4)) multiplexer_23 (.in0(4'b0000), .in1(demultiplexer_26_out1), .sel(is_jalr));  // open: out
  or or_6 (or_6_out, and_1_out, comparator_10_eq);
  assign or_7_out = multiplexer_14_out | multiplexer_6_out | multiplexer_13_out | multiplexer_11_out | multiplexer_2_out | multiplexer_3_out | multiplexer_4_out | multiplexer_5_out | multiplexer_15_out | multiplexer_7_out | multiplexer_8_out | multiplexer_9_out | multiplexer_10_out | multiplexer_12_out;  // OR_Gate or_7, 4 bits wide
  not not_3 (not_3_out, comparator_1_eq);
  or or_8 (or_8_out, comparator_13_eq, comparator_15_eq, comparator_17_eq, comparator_19_eq);
  and and_2 (and_2_out, not_3_out, or_8_out);
  Comparator #(.width(4)) comparator_28 (.a(4'b0011), .b(or_7_out), .eq(comparator_28_eq));  // open: gt, lt
  Comparator #(.width(4)) comparator_29 (.a(4'b0010), .b(or_7_out), .eq(comparator_29_eq));  // open: gt, lt
  Multiplexer #(.width(4)) multiplexer_24 (.in0(4'b0000), .in1(or_7_out), .out(ALU_code), .sel(or_9_out));
  or or_9 (or_9_out, comparator_1_eq, and_2_out);
  nor nor_1 (Reg_WE, comparator_28_eq, comparator_29_eq);

  assign rs = Instruction[25:21];

  // Notes on the sheet:
  //   Funct: 5-0 
  //   shamt: 10-6
  //   rd: 15-11
  //   rt: 20-16
  //   rs: 25-21
  //   Opcode: 31-26
  //   2009000a
  //   Tyeon Ford and Andy Quach
  //   checks if opcode is 0
  //   R-type
  //   CHECKS FOR STAR I-type INSTRUCTIONS:
  //   CHECKS FOR STAR I-type INSTRUCTIONS:
  //   CHECKS FOR J-TYPE INSTRUCTIONS
  //   REWIRE
  //   imm3 or rd
  //   imm2 or shamt
  //   imm1 or funct
  //   may need to check if it this wire is right here
  //   rd
  //   sll (R)
  //   andi (I)
  //   or (R)
  //   imm3
  //   add (R)
  //   sub (R)
  //   mult (R)
  //   div (R)
  //   mflo (R)
  //   mfhi (R)
  //   srl (R)
  //   slt (R)
  //   and (R)
  //   ori (I)
  //   xor (R)
  //   xori (I)
  //   nor (R)
  //   lui (I)
  //   lw (I)
  //   sw (I)
  //   bne (I)
  //   beq (I) 
  //   j (j)
  //   jal (j)
  //   jr (R)
  //   jalr (R)
  //   in binary based on the instruction
  //   if not R-type,
  //   must be I-type or J-type, so gather imm bits
  //   if R-type,
  //   shamt=0
  //   Everything below this is generating the instruction's code
  //   if R-type, rd -> rd
  //   else (I-type), rt -> rd
  //   either I-type or sll or srl
  //   ALU CODES:
  //   = 0 = 0000
  //   = 1 = 0001
  //   = 2 = 0010
  //   = 3 = 0011
  //   = 4 = 0100
  //   = 5 = 0101 
  //   = 6 = 0110
  //   = 7 = 0111
  //   = 8 = 1000
  //   = 9 = 1001
  //   = 10 = 1010
  //   = 11 = 1011
  //   = 12 = 1100
  //   = 13 = 1101
  //   = 1 if R-type
  //   Final ALU code
  //   = 1 if I-type
  //   if addi, ori, or xori, then use imm.
  //   Generates reg_write_e
  //   writes unless its mult or div
  //   Any I-type will have ALU _code of zero.
  //   unless andi, ori, xori, lui
endmodule
